# Fritzing sketch circut (saved by Fritzing 0.9.2b)
breadboards: 1

parts:
  BAT1 = Battery Holders [package=battery-aaa]
  U5 = SWITCH-SPST-2 [package=switch-spst-vertical]
  S1 = Round Pushbutton
  S2 = Round Pushbutton
  U2 = ESP8266 WiFi Module [part_number=ESP8266]

nets:
  N1: BAT1.-, S1.leg1
  N2: BAT1.+, U5.O, U5.P, U2.CH_PD
  N3: S1.leg0, U2.GPIO_0
  N4: S2.leg0, U2.GPIO_2

custom parts:
  ESP8266 WiFi Module: Generic WiFi Module based on the ESP8266 with onboard PCB antenna and UART communications
